# Fritzing sketch Sketch (saved by Fritzing 0.9.3b)
breadboards: 1

parts:
  Part1 = Arduino Uno (Rev3)
  Node_MCU = NodeMCU V3.0
  DHT11 = DHT11 Humitidy and Temperature Sensor
  R2 = Resistor [tolerance=±5% resistance=10k package="0603 [SMD]"]
  R3 = Resistor [tolerance=±5% resistance=220 package="0603 [SMD]"]
  LDR = Photocell (LDR) [package=THT]
  LCD_with_I2C = LCD1602-I2C
  Part4 = FC-28 Soil Hygrometer Module - Probe
  Part5 = FC-28 Soil Hygrometer Module

nets:
  N1: Part1.A0, R2.Pin_1, LDR.pin_0
  N2: Part1.A1, Part5.AO
  N3: Part1.A4/SDA, LCD_with_I2C.SDA
  N4: Part1.A5/SCL, LCD_with_I2C.SCL
  N5: Part1.D5_PWM, Node_MCU.D5
  N6: Part1.D6_PWM, Node_MCU.D6
  N7: Part1.D7, DHT11.DATA, R3.Pin_0
  VCC: DHT11.VDD, R3.Pin_1, LDR.pin_1, LCD_with_I2C.VCC, Part5.VCC
  GND: DHT11.GND, R2.Pin_0, LCD_with_I2C.GND, Part5.GND
  N8: Part4.POS, Part5.POS
  N9: Part4.NEG, Part5.NEG

custom parts:
  NodeMCU V3.0: ESP8266 based NodeMCU
  DHT11 Humitidy and Temperature Sensor: DHT11 Humidity and Temperature Sensor
  LCD1602-I2C: A standard character display, usually with 2x16 characters. Comes in many colors with LCM1602 IIC attached.
  FC-28 Soil Hygrometer Module - Probe: The FC-28 is a soil hygrometer module that uses the Texas Instruments LM393 comparator chip to provide an analog measurement of soil humidity.
  FC-28 Soil Hygrometer Module: The FC-28 is a soil hygrometer module that uses the Texas Instruments LM393 comparator chip to provide an analog measurement of soil humidity. The digital output is high when soil moisture is over a certain threshold, as determined by adjusting the potentiometer.

// code stored in the sketch: Node.ino
#include <ESP8266WiFi.h>
#include <WiFiClient.h>
#include <ESP8266WebServer.h>
#include <ESP8266HTTPClient.h>

/* Set these to your desired credentials. */
const char *ssid = "Peace squad";  //ENTER YOUR WIFI SETTINGS
const char *password = "dhaka1207";

const char *host = "192.168.0.107";

#include <SoftwareSerial.h>
SoftwareSerial s(D6, D5);

char data;
String str;
void setup() {
  Serial.begin(9600);
  s.begin(9600);

  // Wifi Setup
  WifiSetup();
}
void loop() {
  receiver();
  
}

void sendToServer(String post){
  HTTPClient http;    //Declare object of class HTTPClient
 
  http.begin("https://api-tanveer.herokuapp.com/eco-friend/insert.php");//Specify request destination
  http.addHeader("Content-Type", "application/x-www-form-urlencoded");    //Specify content-type header
 
  int httpCode = http.POST(post);   //Send the request
  String payload = http.getString();    //Get the response payload

  if(httpCode != 200){
    Serial.println(httpCode);   //Print HTTP return code  
  }
  
  Serial.println(payload);    //Print request response payload
 
  http.end();  //Close connection
  
  delay(2000);  //Post Data at every 5 seconds
}

void receiver(){
  s.write("s");
  if (s.available() > 0) {
    str = "";
    do {
      data = s.read();
      if(char(data) == '?'){
        str+= '&';
      }
      else if (char(data) != '?') {
        str += data;
      }
      

      delay(10);
    } while (char(data) != '\n');
  }
  Serial.println(str);
  sendToServer(str);
  delay(500);
}
void WifiSetup() {
  WiFi.mode(WIFI_OFF);        //Prevents reconnection issue (taking too long to connect)
  delay(1000);
  WiFi.mode(WIFI_STA);        //This line hides the viewing of ESP as wifi hotspot

  WiFi.begin(ssid, password);     //Connect to your WiFi router
  Serial.println("");

  Serial.print("Connecting");
  // Wait for connection
  while (WiFi.status() != WL_CONNECTED) {
    delay(500);
    Serial.print(".");
  }
  //If connection successful show IP address in serial monitor
  Serial.println("");
  Serial.print("Connected to ");
  Serial.println(ssid);
  Serial.print("IP address: ");
  Serial.println(WiFi.localIP());  //IP address assigned to your ESP
}

// code stored in the sketch: UNO.ino
// Libraries
#include <SoftwareSerial.h>
#include <LiquidCrystal_I2C.h>
#include <dht.h>
dht DHT;


// Pin setup
LiquidCrystal_I2C lcd(0x3F, 2,1,0,4,5,6,7,3, POSITIVE); // LCD
#define DHT11_PIN 7																			// DHT
const int ldrPin = A0;																	// LDR
int moistPin = A1;																			// Soil Moisture
SoftwareSerial s(5, 6);																	// Node MCU Serial Communication

int tmp, lux, moist, hmd = 0;														// Initial variables for sensor

/* Serial lists
 *	UNO Serial 115200
 *	Node Serial 9600
 */

void setup() {
	// Pinsetup
	pinMode(ldrPin, INPUT);
	// DHT & Soil moisture sensore doesn't need pin setup
	
  // Own Serial
  Serial.begin(115200);

  // NodeMCU Serial
  s.begin(9600);

	// Boot msg
  Serial.print("Device Booting");
	lcd.print("Device Booting");
  for(int i=0; i<5; i++){
    Serial.print(".");
		lcd.print(".");
    delay(500);
  }
	lcd.clear();
  Serial.println();
}

void loop() {
  Light();
  Temp();
  Moist();
  transmitter();
	Print();
}

void Light(){
  lux = analogRead(ldrPin); // read the value from the sensor
  int ldrStatus= 0;
  Serial.println("Light: "+ String(lux));
  return;
}

void Temp(){
  int chk = DHT.read11(DHT11_PIN);
  tmp = DHT.temperature;
  Serial.println("Temp: "+String(tmp)+ String((char)223)+"C");
  hmd = DHT.humidity;
  Serial.println("Humid: "+String(hmd)+ "%");
  return;
}

void Moist(){
   moist= analogRead(moistPin);
//   moist = map(moist,550,0,0,100);
	 moist = (100 - ((moist/1023.00) *100);

   Serial.println("Moist: "+String(moist)+"%");
}

void transmitter(){
  String data = "h="+String(hmd)+"&m="+String(moist)+"&l="+String(lux)+"&t="+String(tmp)+"\n";
  
  int sz = data.length();
  for (int i = 0; i < sz; i++) {
    if (s.available() > 0) {
      s.write(data[i]);
      delay(10);
    }
    //  if(s.available()>0){
    //    s.write("c");
  }
  Serial.println(data);
  delay(500);
}

void Print(){
  lcd.clear();
//  lcd.print("Home Forestation!");
  lcd.setCursor(0,0);
	lcd.print("Hum: "+String(hmd)+"%; Soil="+String(moist)+"%");
	Serial.println("Hum: "+String(hmd)+"%; Soil="+String(moist)+"%");
	lcd.setCursor(0,1);
	lcd.print("lght="+String(lux)+"; tmp="+String(tmp)+String((char)223)+"C");
	Serial.println("lght="+String(lux)+"; tmp="+String(tmp)+String((char)223)+"C");

//  BT.println(sen+": "+String(var)+" "+unit);
  delay(2000);
}
